# Fritzing sketch Circuit_Diagram (saved by Fritzing 1.0.2b)
breadboards: 2

parts:
  Part1 = Arduino Uno (Rev3) - ICSP
  Mod1 = Raspberry Pi 4B
  S1 = H-Bridge with L298N
  S2 = H-Bridge with L298N
  M1 = Stepper Motor - Bipolar
  Mod2 = YL-99 Limit switch and LED
  Mod3 = YL-99 Limit switch and LED
  L2 = Solenoid
  L3 = Solenoid
  L4 = Solenoid
  D3 = Rectifier Diode [part_number=1N4001 package="Melf DO-213 AB [SMD]"]
  D4 = Rectifier Diode [part_number=1N4001 package="Melf DO-213 AB [SMD]"]
  D5 = Rectifier Diode [part_number=1N4001 package="Melf DO-213 AB [SMD]"]
  R1 = Resistor [tolerance=±5% resistance=10000 package="2512 [SMD]"]
  R2 = Resistor [tolerance=±5% resistance=10000 package="2512 [SMD]"]
  Q2 = TRANSISTOR_NPN [package=to-92]
  Q3 = TRANSISTOR_NPN [package=to-92]

nets:
  N1: Part1.ICSP_MISO, Part1.D12/MISO, Mod3.OUT, R1.Pin_0
  N2: Part1.ICSP_MOSI, Part1.D11_PWM/MOSI, S1.IN1
  GND: Part1.GND, S1.GND, S2.GND, Mod2.GND, Mod3.GND, L2.pin1, L3.pin1, L4.pin1, D3.anode, D4.anode, D5.anode, R1.Pin_1, R2.Pin_1
  N3: Part1.D8, S1.IN4
  N4: Part1.D9_PWM, S1.IN3
  N5: Part1.D10_PWM/SS, S1.IN2
  N6: Part1.D13/SCK, Mod2.OUT, R2.Pin_0
  3V3: Part1.A4/SDA, Mod1.3V3, Mod1.5V, Mod1.GPIO2
  N7: Part1.A5/SCL, Mod1.GPIO3, Mod1.GND, Mod1.GPIO4, Mod1.GPIO14
  N8: Part1.D2, Q3.B
  N9: Part1.D3_PWM, Q2.B
  N10: Part1.D4, S2.IN1
  N11: Part1.D5_PWM, S2.IN2
  N12: Part1.D6_PWM, S2.IN3
  N13: Part1.D7, S2.IN4
  VCC: Part1.5V, Mod2.VCC, Mod3.VCC
  12V: Part1.VIN, S1.12V, S2.12V
  N14: S1.ENA, Q2.E
  N15: S1.ENB, Q3.E
  N16: S1.M1-01, M1.A
  N17: S1.M1-02, M1.C
  N18: S1.M2-01, M1.D
  N19: S1.M2-02, M1.B
  N20: S1.ENA-5V, Q2.C
  N21: S1.ENB-5V, Q3.C
  N22: S2.ENA, S2.ENA-5V
  N23: S2.ENB, S2.ENB-5V
  N24: S2.M1-01, L3.pin2, D3.cathode
  N25: S2.M1-02, L2.pin2, D4.cathode
  N26: S2.M2-02, L4.pin2, D5.cathode

notes:
  Vin: 12 Volts
  GND

custom parts:
  H-Bridge with L298N: h-bridge
